# Fritzing sketch BeetleBot_Wiring (saved by Fritzing 1.0.4)
breadboards: 1

parts:
  M1 = DOIT Esp32 DevKit v1 (30 pins long, 11 pins width) [part_number=ESP32S-PIN30]
  Motor1 = Dagu DGServo 9g (End View) [part_number=RS001B]
  Motor3 = Dagu DGServo 9g (End View) [part_number=RS001B]
  Motor4 = Dagu DGServo 9g (End View) [part_number=RS001B]
  Motor2 = Dagu DGServo 9g (End View) [part_number=RS001B]
  Motor5 = Dagu DGServo 9g (End View) [part_number=RS001B]
  Motor6 = Dagu DGServo 9g (End View) [part_number=RS001B]
  Motor7 = Dagu DGServo 9g (End View) [part_number=RS001B]
  Motor9 = Dagu DGServo 9g (End View) [part_number=RS001B]
  Motor17 = Dagu DGServo 9g (End View) [part_number=RS001B]
  Motor16 = Dagu DGServo 9g (End View) [part_number=RS001B]
  Motor14 = Dagu DGServo 9g (End View) [part_number=RS001B]
  Motor10 = Dagu DGServo 9g (End View) [part_number=RS001B]
  Motor12 = Dagu DGServo 9g (End View) [part_number=RS001B]
  Motor11 = Dagu DGServo 9g (End View) [part_number=RS001B]
  Motor13 = Dagu DGServo 9g (End View) [part_number=RS001B]
  Motor15 = Dagu DGServo 9g (End View) [part_number=RS001B]
  Motor18 = Dagu DGServo 9g (End View) [part_number=RS001B]
  Servo_Multiplexer = Adafruit PCA9685 PWM/Servo Breakout [part_number=815]
  Sensor_Multiplexer = Adafruit TCA9548A
  Sensor8 = Adafruit VL53L1X [part_number="Adafruit #3967"]
  Sensor7 = Adafruit VL53L1X [part_number="Adafruit #3967"]
  Sensor2 = Adafruit VL53L1X [part_number="Adafruit #3967"]
  Sensor3 = Adafruit VL53L1X [part_number="Adafruit #3967"]
  MotorClaw = Dagu DGServo 9g (End View) [part_number=RS001B]
  Male_XT60 = XT60 Connector [package=THT]
  Female_XT60 = XT60 Connector [package=THT]
  U2 = LM2596 step down module
  Motor8 = Dagu DGServo 9g (End View) [part_number=RS001B]
  Mod1 = 2S-BMS
  U4 = LIPO-1000mAh [package=lipo-1000]
  Female_XT61 = XT60 Connector [package=THT]
  Male_XT61 = XT60 Connector [package=THT]
  S1 = Taiway 100-SP-X-T1 SPDT Miniature Toggle Switch [part_number=100-SP-X-T1-0-0-B1-M2 package=THT]

nets:
  GND: M1.GND, Motor1.gnd, Motor3.gnd, Motor4.gnd, Motor2.gnd, Motor5.gnd, Motor6.gnd, Motor17.gnd, Motor16.gnd, Motor14.gnd, Motor10.gnd, Motor12.gnd, Motor11.gnd, Motor15.gnd, Motor18.gnd, Servo_Multiplexer.GND, Sensor_Multiplexer.GND, Sensor7.GND, Sensor2.GND, Sensor3.GND, MotorClaw.gnd, Motor8.gnd
  N1: M1.D18, Motor7.pulse
  N2: M1.D19, Motor13.pulse
  N3: M1.D21, Servo_Multiplexer.SDA, Sensor_Multiplexer.INPUTSDA
  N4: M1.D22, Servo_Multiplexer.SCL, Sensor_Multiplexer.INPUTSCL
  N5: M1.D23, Motor9.pulse
  VCC: M1.VIN, Servo_Multiplexer.VCC, Sensor_Multiplexer.VCC, Sensor8.VCC, Sensor7.VCC, Sensor2.VCC
  VCC_2: Motor1.vcc, Motor3.vcc, Motor4.vcc, Motor2.vcc, Motor5.vcc, Motor6.vcc, Motor17.vcc, Motor16.vcc, Motor14.vcc, Motor10.vcc, Motor12.vcc, Motor11.vcc, Motor15.vcc, Motor18.vcc, Servo_Multiplexer.5.0V, MotorClaw.vcc, Motor8.vcc
  N6: Motor1.pulse, Servo_Multiplexer.PWM15
  N7: Motor3.pulse, Servo_Multiplexer.PWM13
  N8: Motor4.pulse, Servo_Multiplexer.PWM7
  N9: Motor2.pulse, Servo_Multiplexer.PWM2
  N10: Motor5.pulse, Servo_Multiplexer.PWM1
  N11: Motor6.pulse, Servo_Multiplexer.PWM0
  N12: Motor17.pulse, Servo_Multiplexer.PWM4
  N13: Motor16.pulse, Servo_Multiplexer.PWM10
  N14: Motor14.pulse, Servo_Multiplexer.PWM3
  N15: Motor10.pulse, Servo_Multiplexer.PWM14
  N16: Motor12.pulse, Servo_Multiplexer.PWM9
  N17: Motor11.pulse, Servo_Multiplexer.PWM6
  N18: Motor15.pulse, Servo_Multiplexer.PWM8
  N19: Motor18.pulse, Servo_Multiplexer.PWM11
  N20: Servo_Multiplexer.PWM5, MotorClaw.pulse
  N21: Servo_Multiplexer.PWM12, Motor8.pulse
  N22: Sensor_Multiplexer.2SDA, Sensor2.SDA
  N23: Sensor_Multiplexer.2SCL, Sensor2.SCL
  N24: Sensor_Multiplexer.6SDA, Sensor3.SDA
  N25: Sensor_Multiplexer.6SCL, Sensor3.SCL
  N26: Sensor_Multiplexer.0SDA, Sensor8.SDA
  N27: Sensor_Multiplexer.0SCL, Sensor8.SCL
  N28: Sensor_Multiplexer.1SDA, Sensor7.SDA
  N29: Sensor_Multiplexer.1SCL, Sensor7.SCL
  N30: Male_XT60.GND, Mod1.pin2
  N31: Male_XT60.VCC, Mod1.pin1
  N32: Female_XT60.GND, U4.-
  N33: Female_XT60.VCC, U4.+
  N34: U2.IN+, Female_XT61.VCC
  N35: U2.IN-, U2.OUT-, Female_XT61.GND
  N36: Mod1.pin3#2, Male_XT61.GND
  N37: Mod1.pin3#3, S1.L2
  N38: Male_XT61.VCC, S1.L1

custom parts:
  DOIT Esp32 DevKit v1 (30 pins long, 11 pins width): The DOIT Esp32 DevKit v1 is one of the development board created by DOIT to evaluate the ESP-WROOM-32 module. It is based on the ESP32 microcontroller that boasts Wifi, Bluetooth, Ethernet and Low Power support all in a single chip. (vanepp) made breadboard work, adjusted pin numbering and labels and reduced size of schematic and cleaned up pcb. This chip is 30pins long (2 x15) and 11 pins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
  Adafruit PCA9685 PWM/Servo Breakout: Using only two pins, control 16 free-running PWM outputs! I2C-controlled PWM driver with a built in clock. Unlike the TLC5940 family, you do not need to continuously send it signal tying up your microcontroller, its completely free running! 5V compliant, which means you can control it from a 3.3V microcontroller and still safely drive up to 6V outputs (this is good for when you want to control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
  Adafruit TCA9548A: You just found the perfect I2C sensor, and you want to wire up two or three or more of them to your Arduino when you realize "Uh oh, this chip has a fixed I2C address, and from what I know about I2C, you cannot have two devices with the same address on the same SDA/SCL pins!" Are you out of luck? You would be, if you didn't have this ultra-cool TCA9548A 1-to-8 I2C multiplexer! Finally, a way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
  Adafruit VL53L1X: The Adafruit VL53L1X Time of Flight Distance Sensor (also known as VL53L1CX) is a Time of Flight distance sensor that has a massive 4 meter range and LIDAR-like precision. The sensor contains a very tiny invisible laser source and a matching sensor. The VL53L1X can detect the "time of flight", or how long the light has taken to bounce back to the sensor. Since it uses a very narrow light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
  XT60 Connector: Yellow XT60 connector for high current loads up to 40A
  LM2596 step down module: LM2596 DC-DC step down power supply module 3 A.
  2S-BMS: 2S-BMS LIPO battery charger / protection unit. Note pcb does not match the board as it will likely connect with wires, so pcb is 5 pads suitable for .1in header pins.
